// Logisim project Main.circ as structural Verilog
module XOR_Gate (
  input  A,
  input  B,
  output Out
);

  wire and_1_out, and_2_out, not_1_out, not_2_out;

  and and_1 (and_1_out, A, not_1_out);
  not not_1 (not_1_out, B);
  not not_2 (not_2_out, A);
  and and_2 (and_2_out, not_2_out, B);
  or or_1 (Out, and_1_out, and_2_out);
endmodule

module Half_Adder (
  input  A,
  input  B,
  output Sum,
  output Cout
);

  XOR_Gate xor_1 (.A(A), .B(B), .Out(Sum));
  and and_1 (Cout, A, B);
endmodule

module Full_Adder (
  input  A,
  input  B,
  input  Cin,
  output Sum,
  output Cout
);

  wire half_adder_1_cout, half_adder_1_sum, half_adder_2_cout;

  Half_Adder half_adder_1 (.A(A), .B(B), .Sum(half_adder_1_sum), .Cout(half_adder_1_cout));
  Half_Adder half_adder_2 (.A(half_adder_1_sum), .B(Cin), .Sum(Sum), .Cout(half_adder_2_cout));
  or or_1 (Cout, half_adder_2_cout, half_adder_1_cout);
endmodule

module _2_Mux (
  input  A,
  input  B,
  input  Select,
  output Out
);

  wire and_1_out, and_2_out, not_1_out;

  and and_1 (and_1_out, A, not_1_out);
  not not_1 (not_1_out, Select);
  and and_2 (and_2_out, B, Select);
  or or_1 (Out, and_1_out, and_2_out);
endmodule

module _4_Mux (
  input  A,
  input  B,
  input  C,
  input  D,
  input  S0,
  input  S1,
  output Out
);

  wire n2_mux_1_out, n2_mux_2_out;

  _2_Mux u_2_mux_1 (.A(A), .B(B), .Select(S0), .Out(n2_mux_1_out));
  _2_Mux u_2_mux_2 (.A(C), .B(D), .Select(S0), .Out(n2_mux_2_out));
  _2_Mux u_2_mux_3 (.A(n2_mux_1_out), .B(n2_mux_2_out), .Select(S1), .Out(Out));
endmodule

module _1_bit_ALU (
  input  A,
  input  B,
  input  Cin,
  input  S1,
  input  S0,
  output Out,
  output Cout
);

  wire and_1_out, full_adder_1_sum, or_1_out;

  and and_1 (and_1_out, A, B);
  or or_1 (or_1_out, A, B);
  Full_Adder full_adder_1 (.A(A), .B(B), .Cin(Cin), .Sum(full_adder_1_sum), .Cout(Cout));
  _4_Mux u_4_mux_1 (.A(full_adder_1_sum), .B(and_1_out), .C(or_1_out), .S0(S0), .S1(S1), .Out(Out));  // open: D
endmodule

module _4_bit_ALU (
  input  Cin,
  input  S1,
  input  S0,
  input  [3:0] A,
  input  [3:0] B,
  output [3:0] Out,
  output Cout
);

  wire n1_bit_alu_1_cout, n1_bit_alu_2_cout, n1_bit_alu_3_cout;

  _1_bit_ALU u_1_bit_alu_1 (.A(A[0]), .B(B[0]), .Cin(Cin), .S1(S1), .S0(S0), .Out(Out[0]), .Cout(n1_bit_alu_1_cout));
  _1_bit_ALU u_1_bit_alu_2 (
    .A(A[1]), .B(B[1]), .Cin(n1_bit_alu_1_cout), .S1(S1), .S0(S0), .Out(Out[1]), .Cout(n1_bit_alu_2_cout));
  _1_bit_ALU u_1_bit_alu_3 (
    .A(A[2]), .B(B[2]), .Cin(n1_bit_alu_2_cout), .S1(S1), .S0(S0), .Out(Out[2]), .Cout(n1_bit_alu_3_cout));
  _1_bit_ALU u_1_bit_alu_4 (.A(A[3]), .B(B[3]), .Cin(n1_bit_alu_3_cout), .S1(S1), .S0(S0), .Out(Out[3]), .Cout(Cout));
endmodule

module Full_1_bit__4_opp_ALU (
  input  A,
  input  B,
  input  Cin,
  input  S1,
  input  S0,
  output Out,
  output Cout
);

  wire and_1_out, full_adder_1_cout, full_adder_1_sum, n1_bit_alu_1_cout, n1_bit_alu_1_out, not_1_out;

  not not_1 (not_1_out, B);
  _1_bit_ALU u_1_bit_alu_1 (
    .A(A), .B(B), .Cin(Cin), .S1(S1), .S0(S0), .Out(n1_bit_alu_1_out), .Cout(n1_bit_alu_1_cout));
  and and_1 (and_1_out, S1, S0);
  Full_Adder full_adder_1 (.A(A), .B(not_1_out), .Cin(Cin), .Sum(full_adder_1_sum), .Cout(full_adder_1_cout));
  _2_Mux u_2_mux_1 (.A(n1_bit_alu_1_out), .B(full_adder_1_sum), .Select(and_1_out), .Out(Out));
  _2_Mux u_2_mux_2 (.A(n1_bit_alu_1_cout), .B(full_adder_1_cout), .Select(and_1_out), .Out(Cout));
endmodule

module Full_4_bit__4_opp_ALU (
  input  S1,
  input  S0,
  input  [3:0] A,
  input  [3:0] B,
  output [3:0] out_5,
  output Cout
);

  wire and_1_out, full_1_bit_4_opp_alu_1_cout, full_1_bit_4_opp_alu_2_cout, full_1_bit_4_opp_alu_3_cout;

  and and_1 (and_1_out, S1, S0);
  Full_1_bit__4_opp_ALU full_1_bit_4_opp_alu_1 (
    .A(A[0]), .B(B[0]), .S1(S1), .S0(S0), .Out(out_5[0]), .Cout(full_1_bit_4_opp_alu_1_cout), .Cin(and_1_out));
  Full_1_bit__4_opp_ALU full_1_bit_4_opp_alu_2 (
    .A(A[1]), .B(B[1]), .S1(S1), .S0(S0), .Out(out_5[1]), .Cout(full_1_bit_4_opp_alu_2_cout),
    .Cin(full_1_bit_4_opp_alu_1_cout));
  Full_1_bit__4_opp_ALU full_1_bit_4_opp_alu_3 (
    .A(A[2]), .B(B[2]), .S1(S1), .S0(S0), .Out(out_5[2]), .Cout(full_1_bit_4_opp_alu_3_cout),
    .Cin(full_1_bit_4_opp_alu_2_cout));
  Full_1_bit__4_opp_ALU full_1_bit_4_opp_alu_4 (
    .A(A[3]), .B(B[3]), .S1(S1), .S0(S0), .Out(out_5[3]), .Cout(Cout), .Cin(full_1_bit_4_opp_alu_3_cout));
endmodule

module SR_latch (
  input  R,
  input  S,
  output Q,
  output Q_prime
);

  wire or_1_out, or_2_out;

  or or_1 (or_1_out, R, Q_prime);
  or or_2 (or_2_out, Q, S);
  not not_1 (Q, or_1_out);
  not not_2 (Q_prime, or_2_out);
endmodule

module D_latch (
  input  D,
  input  E,
  output Q
);

  wire and_1_out, and_2_out, not_1_out;

  not not_1 (not_1_out, D);
  and and_1 (and_1_out, not_1_out, E);
  and and_2 (and_2_out, D, E);
  SR_latch sr_latch_1 (.R(and_1_out), .S(and_2_out), .Q(Q));  // open: Q_prime
endmodule

module D_flip_flop (
  input  D,
  input  WE,
  input  CLK,
  output Q
);

  wire d_latch_1_q, n2_mux_1_out, not_1_out;

  _2_Mux u_2_mux_1 (.A(Q), .B(D), .Select(WE), .Out(n2_mux_1_out));
  D_latch d_latch_1 (.D(n2_mux_1_out), .E(not_1_out), .Q(d_latch_1_q));
  not not_1 (not_1_out, CLK);
  D_latch d_latch_2 (.D(d_latch_1_q), .E(CLK), .Q(Q));
endmodule

module register_file__4_bits (
  input  [3:0] Data_In,
  input  CLK,
  input  WE,
  output [3:0] Data_Out
);

  D_flip_flop d_flip_flop_1 (.D(Data_In[0]), .WE(WE), .Q(Data_Out[0]), .CLK(CLK));
  D_flip_flop d_flip_flop_2 (.D(Data_In[1]), .WE(WE), .Q(Data_Out[1]), .CLK(CLK));
  D_flip_flop d_flip_flop_3 (.D(Data_In[2]), .WE(WE), .Q(Data_Out[2]), .CLK(CLK));
  D_flip_flop d_flip_flop_4 (.D(Data_In[3]), .WE(WE), .Q(Data_Out[3]), .CLK(CLK));
endmodule

module register_file__8_4_bits (
  input  [3:0] Data_In,
  input  [2:0] WA,
  input  Enable,
  input  [2:0] Read_Addr_1,
  input  [2:0] Read_Addr_2,
  input  CLK,
  output [3:0] Data_1_Out,
  output [3:0] Data_2_Out
);

  register_file__4_bits register_file_4_bits_1 (.Data_In(Data_In), .WE(CLK));  // open: CLK, Data_Out
  register_file__4_bits register_file_4_bits_2 (.Data_In(Data_In), .WE(CLK));  // open: CLK, Data_Out
  register_file__4_bits register_file_4_bits_3 (.Data_In(Data_In), .WE(CLK));  // open: CLK, Data_Out
  register_file__4_bits register_file_4_bits_4 (.Data_In(Data_In), .WE(CLK));  // open: CLK, Data_Out
  register_file__4_bits register_file_4_bits_5 (.Data_In(Data_In), .WE(CLK));  // open: CLK, Data_Out
  register_file__4_bits register_file_4_bits_6 (.Data_In(Data_In), .WE(CLK));  // open: CLK, Data_Out
  register_file__4_bits register_file_4_bits_7 (.Data_In(Data_In), .WE(CLK));  // open: CLK, Data_Out
  register_file__4_bits register_file_4_bits_8 (.Data_In(Data_In), .WE(CLK));  // open: CLK, Data_Out
endmodule

module _2_mux__4bits (
  input  [3:0] A,
  input  [3:0] B,
  input  Select,
  output [3:0] out_4
);

  _2_Mux u_2_mux_1 (.A(A[0]), .B(B[0]), .Select(Select), .Out(out_4[0]));
  _2_Mux u_2_mux_2 (.A(A[1]), .B(B[1]), .Select(Select), .Out(out_4[1]));
  _2_Mux u_2_mux_3 (.A(A[2]), .B(B[2]), .Select(Select), .Out(out_4[2]));
  _2_Mux u_2_mux_4 (.A(A[3]), .B(B[3]), .Select(Select), .Out(out_4[3]));
endmodule

module _4_mux__4_bits (
  input  [3:0] A,
  input  [3:0] B,
  input  [3:0] C,
  input  [3:0] D,
  input  [1:0] Select,
  output [3:0] Out
);

  wire [3:0] n2_mux_4bits_1_out_4, n2_mux_4bits_2_out_4;

  _2_mux__4bits u_2_mux_4bits_1 (.A(A), .B(B), .Select(Select[0]), .out_4(n2_mux_4bits_1_out_4));
  _2_mux__4bits u_2_mux_4bits_2 (.A(C), .B(D), .Select(Select[0]), .out_4(n2_mux_4bits_2_out_4));
  _2_mux__4bits u_2_mux_4bits_3 (.A(n2_mux_4bits_1_out_4), .B(n2_mux_4bits_2_out_4), .Select(Select[1]), .out_4(Out));
endmodule

module _8_mux__4_bits (
  input  [3:0] A,
  input  [3:0] B,
  input  [3:0] C,
  input  [3:0] D,
  input  [3:0] E,
  input  [3:0] F,
  input  [3:0] G,
  input  [3:0] H
);

  _4_mux__4_bits u_4_mux_4_bits_1 ();  // open: A, B, C, D, Select, Out
  _4_mux__4_bits u_4_mux_4_bits_2 ();  // open: A, B, C, D, Select, Out
  _2_mux__4bits u_2_mux_4bits_1 ();  // open: A, B, Select, out_4
endmodule
